# Fritzing sketch IMU connection (saved by Fritzing 0.9.3b)
breadboards: 1

parts:
  Εξάρτημα1 = Arduino Mega 2560 (Rev3)
  Εξάρτημα2 = InvenSense MPU6050

nets:
  N1: Εξάρτημα1.D21/SCL, Εξάρτημα2.SCL
  N2: Εξάρτημα1.D20/SDA, Εξάρτημα2.SDA
  5V: Εξάρτημα1.5V, Εξάρτημα2.VCC
  GND: Εξάρτημα1.GND, Εξάρτημα2.GND
