# Fritzing sketch Light and buzzer connection (saved by Fritzing 0.9.3b)
breadboards: 1

parts:
  Εξάρτημα1 = Arduino Mega 2560 (Rev3)
  LED = Prolight RGB 3 Watt Star
  Εξάρτημα4 = IFR520 MOS module [package=THT]
  Ηχείο = Piezo Speaker  # not connected
  Εξάρτημα5 = IFR520 MOS module [package=THT]

nets:
  VCC: Εξάρτημα1.5V, Εξάρτημα4.VCC, Εξάρτημα5.VCC
  N1: Εξάρτημα1.D27, Εξάρτημα5.SIG
  N2: Εξάρτημα1.D29, Εξάρτημα4.SIG
  GND: Εξάρτημα1.GND, Εξάρτημα4.GND, Εξάρτημα5.GND
  N3: LED.R-, LED.B-, Εξάρτημα4.V+, Εξάρτημα4.VIN
