# Fritzing sketch PIR connection (saved by Fritzing 0.9.3b)
breadboards: 1

parts:
  Εξάρτημα1 = Arduino Mega 2560 (Rev3)
  PIR1 = PIR sensor

nets:
  5V: Εξάρτημα1.5V, PIR1.VDD
  N1: Εξάρτημα1.D25, PIR1.SIG
  GND: Εξάρτημα1.GND, PIR1.GND
