# Fritzing sketch Rain Sensor connection (saved by Fritzing 0.9.3b)
breadboards: 1

parts:
  Εξάρτημα1 = Arduino Mega 2560 (Rev3)
  YL-83_-_Control_Board1 = YL-83 Rain Sensor - Control Board
  YL-83_-_Detection_Board1 = YL-83 Rain Sensor - Detection Board

nets:
  5V: Εξάρτημα1.5V, YL-83_-_Control_Board1.VCC, YL-83_-_Control_Board1.AO
  GND: Εξάρτημα1.GND, YL-83_-_Control_Board1.GND
  N1: YL-83_-_Control_Board1.POS, YL-83_-_Detection_Board1.POS
  N2: YL-83_-_Control_Board1.NEG, YL-83_-_Detection_Board1.NEG

custom parts:
  YL-83 Rain Sensor - Control Board: The YL-83 is a rain sensor that has more resistance when dry and less resistance when wet. The module runs at 5V.
  YL-83 Rain Sensor - Detection Board: The YL-83 is a rain sensor that has more resistance when dry and less resistance when wet. The module runs at 5V.
