# Fritzing sketch Snow plow full (saved by Fritzing 0.9.3b)
breadboards: 1

parts:
  Εξάρτημα1 = Arduino Mega 2560 (Rev3)
  Μονάδα_IMU = InvenSense MPU6050
  Αισθητήρας_βροχής/χιονιού = YL-83 Rain Sensor - Detection Board
  YL-83_-_Control_Board1 = YL-83 Rain Sensor - Control Board
  Εξάρτημα3 = Adafruit Motor/Stepper/Servo Shield [part_number="Adafruit #1438"]
  Αισθητήρας_θερμοκρασίας = DHT11 module
  Αισθητήρας_απόστασης = HC-SR04 Ultrasonic Distance Sensor
  LED = Prolight RGB 3 Watt Star
  Αισθητήρας_κίνησης = PIR sensor
  Εξάρτημα4 = IFR520 MOS module [package=THT]
  Ηχείο = IFR520 MOS module [package=THT]
  J1 = Piezo Speaker  # not connected
  ULN2003A_-_Stepper_Driver_Board1 = ULN2003A - Stepper Driver Board [package=board]
  Κινητήρας_αλατιέρας = 28BYJ-48 Stepper Motor
  Μπροστά_δεξιά_κινητήρας = DC Motor  # not connected
  Μπροστά_αριστερά_κινητήρας = DC Motor  # not connected
  Πίσω_δεξιά_κινητήρας = DC Motor  # not connected
  Πίσω_αριστερά_κινητήρας = DC Motor  # not connected
  Μπαταρίες_για_οδηγό_κινητήρων = 4 x AAA Battery Mount
  Σέρβο_για_μαχαίρι = Dagu DGServo 9g (Top view) [part_number=RS001B]
  Σέρβο_για_διασκορπισμό_αλατιού = Dagu DGServo 9g (Top view) [part_number=RS001B]

nets:
  N1: Εξάρτημα1.A14, Αισθητήρας_θερμοκρασίας.DATA
  N2: Εξάρτημα1.A15, YL-83_-_Control_Board1.AO
  N3: Εξάρτημα1.D21/SCL, Μονάδα_IMU.SCL
  N4: Εξάρτημα1.D20/SDA, Μονάδα_IMU.SDA
  VCC: Εξάρτημα1.5V, Μονάδα_IMU.VCC, YL-83_-_Control_Board1.VCC, Αισθητήρας_θερμοκρασίας.VCC, Αισθητήρας_απόστασης.VCC, Αισθητήρας_κίνησης.VDD, Εξάρτημα4.VCC, Ηχείο.VCC, ULN2003A_-_Stepper_Driver_Board1.VCC
  N5: Εξάρτημα1.D23, Αισθητήρας_απόστασης.TRIG, Αισθητήρας_απόστασης.ECHO
  N6: Εξάρτημα1.D25, Αισθητήρας_κίνησης.SIG
  N7: Εξάρτημα1.D27, Ηχείο.SIG
  N8: Εξάρτημα1.D29, Εξάρτημα4.SIG
  N9: Εξάρτημα1.D35, ULN2003A_-_Stepper_Driver_Board1.IN1
  N10: Εξάρτημα1.D37, ULN2003A_-_Stepper_Driver_Board1.IN2
  N11: Εξάρτημα1.D39, ULN2003A_-_Stepper_Driver_Board1.IN3
  N12: Εξάρτημα1.D41, ULN2003A_-_Stepper_Driver_Board1.IN4
  GND: Εξάρτημα1.GND, Μονάδα_IMU.GND, YL-83_-_Control_Board1.GND, Αισθητήρας_θερμοκρασίας.GND, Αισθητήρας_απόστασης.GND, Αισθητήρας_κίνησης.GND, Εξάρτημα4.GND, Ηχείο.GND, ULN2003A_-_Stepper_Driver_Board1.GND
  N13: Αισθητήρας_βροχής/χιονιού.POS, YL-83_-_Control_Board1.POS
  N14: Αισθητήρας_βροχής/χιονιού.NEG, YL-83_-_Control_Board1.NEG
  GND_2: Εξάρτημα3.GND, Μπαταρίες_για_οδηγό_κινητήρων.-, Σέρβο_για_μαχαίρι.gnd, Σέρβο_για_διασκορπισμό_αλατιού.gnd
  N15: Εξάρτημα3.VMOTOR, Μπαταρίες_για_οδηγό_κινητήρων.+
  VCC_2: Εξάρτημα3.+5V, Σέρβο_για_μαχαίρι.vcc, Σέρβο_για_διασκορπισμό_αλατιού.vcc
  N16: Εξάρτημα3.D10, Σέρβο_για_μαχαίρι.pulse
  N17: Εξάρτημα3.D9, Σέρβο_για_διασκορπισμό_αλατιού.pulse
  N18: LED.R-, LED.B-, Εξάρτημα4.V+, Εξάρτημα4.VIN
  N19: ULN2003A_-_Stepper_Driver_Board1.BLUE, Κινητήρας_αλατιέρας.RED
  N20: ULN2003A_-_Stepper_Driver_Board1.PINK, Κινητήρας_αλατιέρας.ORANGE
  N21: ULN2003A_-_Stepper_Driver_Board1.YELLOW, Κινητήρας_αλατιέρας.YELLOW
  N22: ULN2003A_-_Stepper_Driver_Board1.ORANGE, Κινητήρας_αλατιέρας.PINK
  N23: ULN2003A_-_Stepper_Driver_Board1.RED, Κινητήρας_αλατιέρας.BLUE

custom parts:
  YL-83 Rain Sensor - Detection Board: The YL-83 is a rain sensor that has more resistance when dry and less resistance when wet. The module runs at 5V.
  YL-83 Rain Sensor - Control Board: The YL-83 is a rain sensor that has more resistance when dry and less resistance when wet. The module runs at 5V.
  Adafruit Motor/Stepper/Servo Shield: The original Adafruit Motorshield kit is one of our most beloved kits, which is why we decided to make something even better. We have upgraded the shield kit to make the bestest, easiest way to drive DC and Stepper motors. This shield will make quick work of your next robotics project! We kept the ability to drive up to 4 DC motors or 2 stepper motors, but added many improvements: Instead of a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
  DHT11 module: DHT11 black pcb module
  ULN2003A - Stepper Driver Board: A common stepper motor driver board based on ULN2003APG darlington array
