# Fritzing sketch Temperature Sensor connection (saved by Fritzing 0.9.3b)
breadboards: 1

parts:
  Εξάρτημα1 = Arduino Mega 2560 (Rev3)
  DHT11_1 = DHT11 module

nets:
  N1: Εξάρτημα1.A14, DHT11_1.DATA
  5V: Εξάρτημα1.5V, DHT11_1.VCC
  GND: Εξάρτημα1.GND, DHT11_1.GND

custom parts:
  DHT11 module: DHT11 black pcb module
