# Fritzing sketch Ultrasonic connection (saved by Fritzing 0.9.3b)
breadboards: 1

parts:
  Εξάρτημα1 = Arduino Mega 2560 (Rev3)
  HC-SR04_Sensor_1 = HC-SR04 Ultrasonic Distance Sensor

nets:
  5V: Εξάρτημα1.5V, HC-SR04_Sensor_1.VCC
  N1: Εξάρτημα1.D23, HC-SR04_Sensor_1.TRIG, HC-SR04_Sensor_1.ECHO
  GND: Εξάρτημα1.GND, HC-SR04_Sensor_1.GND
