# Fritzing sketch mpu6050_to_nano (saved by Fritzing 0.9.3b)
breadboards: 1

parts:
  GY1 = MPU-6050 Board GY-521 [form="♀ (female)" package=THT]
  Εξάρτημα1 = Arduino Nano (Rev3.0)

nets:
  N1: GY1.pin1, Εξάρτημα1.5V
  N2: GY1.pin2, Εξάρτημα1.GND
  N3: GY1.pin3, Εξάρτημα1.A5
  N4: GY1.pin4, Εξάρτημα1.A4

custom parts:
  MPU-6050 Board GY-521: Acelerometro y Giroscopio MPU-6050 Board GY-521
