# Fritzing sketch mpu6050_to_uno (saved by Fritzing 0.9.3b)

parts:
  GY1 = MPU-6050 Board GY-521 [form="♀ (female)" package=THT]
  Εξάρτημα1 = Arduino Uno (Rev3)

nets:
  N1: GY1.pin1, Εξάρτημα1.5V
  N2: GY1.pin2, Εξάρτημα1.GND
  N3: GY1.pin3, Εξάρτημα1.A5/SCL
  N4: GY1.pin4, Εξάρτημα1.A4/SDA

custom parts:
  MPU-6050 Board GY-521: Acelerometro y Giroscopio MPU-6050 Board GY-521
